// Logisim project hw3-3.circ as structural Verilog: 3 circuits, main circuit Black Box Test
module Black_Box_Test (
  input  b3,
  input  b2,
  input  b1,
  input  b0,
  input  a3,
  input  a2,
  input  a1,
  input  a0,
  input  d0,
  input  d1,
  output c_out,
  output s3,
  output s2,
  output s1,
  output s0
);

  ALU alu_1 (
    .d0(d0), .d1(d1), .c_out(c_out), .b3(b3), .b2(b2), .b1(b1), .b0(b0), .a3(a3), .a2(a2), .a1(a1), .a0(a0),
    .s3(s3), .s2(s2), .s1(s1), .s0(s0));

  // Notes on the sheet:
  //   ALU Control d1 d0
  //   00 = add 
  //   01 = sub
  //   10 = dec 
  //   11 = inc 
  //   Black Box Testing of 4-bit ALU
endmodule

// 4-bit ALU
module ALU (
  input  b3,
  input  b2,
  input  b1,
  input  b0,
  input  a3,
  input  a2,
  input  a1,
  input  a0,
  input  d0,
  input  d1,
  output c_out,
  output s3,
  output s2,
  output s1,
  output s0
);

  wire and_1_out, and_2_out, and_3_out, and_4_out, and_5_out, and_6_out, and_7_out, and_8_out, and_9_out,
       and_10_out, and_11_out, and_12_out, full_adder_2_cout, full_adder_3_cout, full_adder_4_cout, or_1_out,
       or_2_out, or_3_out, or_4_out;

  and and_1 (and_1_out, d1, ~d0);  // AND_Gate
  and and_2 (and_2_out, ~d1, d0, ~b3);  // AND_Gate
  or or_1 (or_1_out, and_1_out, and_2_out, and_3_out);
  Full_Adder full_adder_1 (.cin(full_adder_2_cout), .x(a3), .y(or_1_out), .Sum(s3), .cout(c_out));
  and and_3 (and_3_out, ~d0, b3);  // AND_Gate
  and and_4 (and_4_out, d1, ~d0);  // AND_Gate
  and and_5 (and_5_out, ~d1, d0, ~b2);  // AND_Gate
  or or_2 (or_2_out, and_4_out, and_5_out, and_7_out);
  and and_6 (and_6_out, d1, ~d0);  // AND_Gate
  and and_7 (and_7_out, ~d0, b2);  // AND_Gate
  Full_Adder full_adder_2 (.cin(full_adder_3_cout), .x(a2), .y(or_2_out), .Sum(s2), .cout(full_adder_2_cout));
  and and_8 (and_8_out, ~d0, b1);  // AND_Gate
  and and_9 (and_9_out, ~d1, d0, ~b1);  // AND_Gate
  or or_3 (or_3_out, and_6_out, and_9_out, and_8_out);
  and and_10 (and_10_out, d1, ~d0);  // AND_Gate
  Full_Adder full_adder_3 (.cin(full_adder_4_cout), .x(a1), .y(or_3_out), .Sum(s1), .cout(full_adder_3_cout));
  and and_11 (and_11_out, ~d1, d0, ~b0);  // AND_Gate
  or or_4 (or_4_out, and_10_out, and_11_out, and_12_out);
  Full_Adder full_adder_4 (.cin(d0), .x(a0), .y(or_4_out), .Sum(s0), .cout(full_adder_4_cout));
  and and_12 (and_12_out, ~d0, b0);  // AND_Gate

  // Notes on the sheet:
  //   c_in
  //   x3
  //   x2
  //   x1
  //   x0
endmodule

// FA
module Full_Adder (
  input  cin,
  input  x,
  input  y,
  output Sum,
  output cout
);

  wire and_1_out, and_2_out, xor_1_out;

  and and_1 (and_1_out, x, y);
  xor xor_1 (xor_1_out, x, y);
  and and_2 (and_2_out, cin, xor_1_out);
  xor xor_2 (Sum, cin, xor_1_out);
  or or_1 (cout, and_2_out, and_1_out);

  // Notes on the sheet:
  //   Full Adder
endmodule
