// Logisim project hw4.circ as structural Verilog: 1 circuit, main circuit main
module main (
  input  x,
  output z
);

  wire and_1_out, and_2_out, and_3_out, and_4_out, and_5_out, and_6_out, and_7_out, and_8_out, and_9_out,
       and_10_out, button_1_out, clock_1_out, s0_prime_out, s0_q, s1_prime_out, s1_q, s2_prime_out, s2_q;

  Clock clock_1 (.out(clock_1_out));
  Button button_1 (.out(button_1_out));
  and and_1 (and_1_out, ~s2_q, s1_q, ~x);  // AND_Gate
  and and_2 (and_2_out, s2_q, ~s0_q, x);  // AND_Gate
  and and_3 (and_3_out, ~s2_q, s1_q);  // AND_Gate
  and and_4 (and_4_out, s1_q, ~s0_q);  // AND_Gate
  and and_5 (and_5_out, ~s1_q, x);  // AND_Gate
  and and_6 (and_6_out, ~s1_q, s0_q);  // AND_Gate
  and and_7 (and_7_out, s2_q, x);
  and and_8 (and_8_out, s2_q, s0_q);
  and and_9 (and_9_out, s1_q, s0_q, x);
  and and_10 (and_10_out, ~s2_q, s1_q, ~s0_q, ~x);  // AND_Gate
  D_Flip_Flop s2 (.clk(clock_1_out), .D(s2_prime_out), .Q(s2_q), .reset(button_1_out));  // open: Qn, preset, en
  or s2_prime (s2_prime_out, and_1_out, and_2_out);
  or s1_prime (s1_prime_out, ~x, and_3_out, and_4_out);  // OR_Gate
  or s0_prime (s0_prime_out, and_5_out, and_6_out, and_7_out, and_8_out);
  or u_z (z, and_9_out, and_10_out);
  D_Flip_Flop s1 (.clk(clock_1_out), .D(s1_prime_out), .Q(s1_q), .reset(button_1_out));  // open: Qn, preset, en
  D_Flip_Flop s0 (.clk(clock_1_out), .D(s0_prime_out), .Q(s0_q), .reset(button_1_out));  // open: Qn, preset, en

  // Notes on the sheet:
  //   s0
  //   s1
  //   s2
  //   x
  //   s2' *s1*x' + s2*s0' *x
  //   x' + s2' *s1+s1*s0'
  //   s1' *x+s1' *s0+s2*x+s2*s0
  //   s1*s0*x+s2' *s1*s0' *x'
endmodule
